# Fritzing sketch toilet-project (saved by Fritzing 0.9.3b)
breadboards: 1

parts:
  R1 = Photocell (LDR) [package=THT]
  R2 = Resistor [tolerance=±5% resistance=10k package=THT]
  U1 = NodeMCU V1.0
  PIR1 = PIR sensor
  S1 = Pushbutton [package=THT]
  R3 = Resistor [tolerance=±5% resistance=10k package=THT]
  S2 = Pushbutton [package=THT]
  R4 = Resistor [tolerance=±5% resistance=10k package=THT]

nets:
  3V3: R1.pin_0, U1.3V3, PIR1.VDD, S1.leg1, S2.leg1
  N1: R2.Pin_0, U1.A0
  GND: R2.Pin_1, U1.GND, PIR1.GND, R3.Pin_1, R4.Pin_1
  N2: U1.D5, S1.leg0, R3.Pin_0
  N3: U1.D6, PIR1.SIG
  N4: U1.D7, S2.leg0, R4.Pin_0

custom parts:
  NodeMCU V1.0: ESP8266 based NodeMCU
